# Fritzing sketch Full Schematic (saved by Fritzing 0.9.3b)

parts:
  M1 = MPS20N0040D
  LDO_AP2112-3_3 = IC, DIP package, 6 pins [chip_label="LDO AP2112-3.3"]
  Part1 = InvenSense MPU6050
  Battery = LIPO-1000mAh [package=lipo-1000]
  M2 = DOIT Esp32 DevKit v1 (30 pins long, 11 pins width) [part_number=ESP32S-PIN30]
  LDO_AP2112-3_4 = IC, DIP package, 4 pins [chip_label=Buck3V]
  LDO_AP2112-3_5 = IC, DIP package, 6 pins [chip_label=Switch1]
  LDO_AP2112-3_6 = IC, DIP package, 4 pins [chip_label=Pump]
  LDO_AP2112-3_7 = IC, DIP package, 6 pins [chip_label=Switch2]
  LDO_AP2112-3_8 = IC, DIP package, 4 pins [chip_label=Valve]
  M3 = MAX30102
  Temp = gy-906
  LDO_AP2112-3_9 = IC, DIP package, 8 pins [chip_label=Display]
  Pushbutton1 = Pushbutton [package="[SMD]"]
  R1 = Resistor [tolerance=±5% resistance=10k package=THT]
  Pushbutton2 = Pushbutton [package="[SMD]"]
  R2 = Resistor [tolerance=±5% resistance=10k package=THT]

nets:
  VCC: M1.VCC, LDO_AP2112-3_3.pin6, Part1.VCC, M2.3V3, LDO_AP2112-3_5.pin1, M3.VIN, Temp.VIN, LDO_AP2112-3_9.pin7, Pushbutton1.Pin_3, Pushbutton1.Pin_4, Pushbutton2.Pin_3, Pushbutton2.Pin_4
  N1: M1.OUT, M2.D18
  N2: M1.SCK, M2.D19
  GND: M1.GND, LDO_AP2112-3_3.pin2, Part1.GND, Battery.-, M2.GND, LDO_AP2112-3_4.pin2, LDO_AP2112-3_4.pin3, LDO_AP2112-3_5.pin2, LDO_AP2112-3_6.pin1, LDO_AP2112-3_7.pin2, LDO_AP2112-3_8.pin1, M3.GND, Temp.GND, LDO_AP2112-3_9.pin6, R1.Pin_1, R2.Pin_1
  N3: LDO_AP2112-3_3.pin1, LDO_AP2112-3_3.pin3, Battery.+, LDO_AP2112-3_4.pin1
  N4: Part1.SCL, M2.D22, M3.SCL, Temp.SCL
  N5: Part1.SDA, M2.D21, M3.SDA, Temp.SDA
  N6: M2.D15, LDO_AP2112-3_9.pin8
  N7: M2.RX2, LDO_AP2112-3_7.pin3
  N8: M2.TX2, LDO_AP2112-3_5.pin3
  N9: M2.D34, Pushbutton1.Pin_1, Pushbutton1.Pin_2, R1.Pin_0
  N10: M2.D35, Pushbutton2.Pin_1, Pushbutton2.Pin_2, R2.Pin_0
  N11: M2.D25, LDO_AP2112-3_9.pin1
  N12: M2.D26, LDO_AP2112-3_9.pin2
  N13: M2.D14, LDO_AP2112-3_9.pin3
  N14: M2.D13, LDO_AP2112-3_9.pin4
  N15: LDO_AP2112-3_4.pin4, LDO_AP2112-3_5.pin5, LDO_AP2112-3_7.pin5
  N16: LDO_AP2112-3_5.pin6, LDO_AP2112-3_6.pin4
  N17: LDO_AP2112-3_7.pin6, LDO_AP2112-3_8.pin4

custom parts:
  MPS20N0040D: MPS20N0040D Sphygmomanometer 0-40kPa Differential Air Pressure Sensor / HX710B ADC Module This module couples a MPS20N0040D sphygmomanometer air pressure sensor module with an HX710B analog-to-digital converter IC. It can be powered from a 3.3V or 5V source, with a claimed measurement range of 0-40kPa. It uses a proprietary 2-wire communication protocol and is thus not I2C compatible. Links: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
  DOIT Esp32 DevKit v1 (30 pins long, 11 pins width): The DOIT Esp32 DevKit v1 is one of the development board created by DOIT to evaluate the ESP-WROOM-32 module. It is based on the ESP32 microcontroller that boasts Wifi, Bluetooth, Ethernet and Low Power support all in a single chip. (vanepp) made breadboard work, adjusted pin numbering and labels and reduced size of schematic and cleaned up pcb. This chip is 30pins long (2 x15) and 11 pins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
  MAX30102: Oximeter module using the MAX30102 chip. You may wish to read (and check your module) this post on power problems with these modules: https://reedpaper.wordpress.com/2018/08/22/pulse-oximeter-max30100-max30102-how-to-fix-wrong-board/ . As usual, if you want the mounting holes in pcb, you need to drag a hole over the pad in silkscreen to actually drill the hole (by default they are not drilled)
  gy-906: gy-906 Non-contact PIR I2C interface temperature sensor breakout board.
