# Fritzing sketch accelero_pressure (saved by Fritzing 0.9.3b)

parts:
  ESP32_DEVKIT1 = MH-ET LIVE ESP32 DEVKIT 38 pins
  M1 = MPS20N0040D
  LDO_AP2112-3_3 = IC, DIP package, 6 pins [chip_label=IC]
  Part1 = InvenSense MPU6050
  U1 = LIPO-1000mAh [package=lipo-1000]

nets:
  VCC: ESP32_DEVKIT1.3V3, M1.VCC, LDO_AP2112-3_3.pin6, Part1.VCC
  GND: ESP32_DEVKIT1.GND, M1.GND, LDO_AP2112-3_3.pin2, Part1.GND, U1.-
  N1: ESP32_DEVKIT1.IO22, Part1.SCL
  N2: ESP32_DEVKIT1.IO21, Part1.SDA
  N3: ESP32_DEVKIT1.IO19, M1.SCK
  N4: ESP32_DEVKIT1.IO18, M1.OUT
  N5: LDO_AP2112-3_3.pin1, LDO_AP2112-3_3.pin3, U1.+

custom parts:
  MH-ET LIVE ESP32 DEVKIT 38 pins: http://mh.nodebb.com/topic/2/mh-et-live-esp32-devkit
  MPS20N0040D: MPS20N0040D Sphygmomanometer 0-40kPa Differential Air Pressure Sensor / HX710B ADC Module This module couples a MPS20N0040D sphygmomanometer air pressure sensor module with an HX710B analog-to-digital converter IC. It can be powered from a 3.3V or 5V source, with a claimed measurement range of 0-40kPa. It uses a proprietary 2-wire communication protocol and is thus not I2C compatible. Links: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
